// Logisim project CS1409_U201414803_许荣仁_alu.circ as structural Verilog: 7 circuits, main circuit ALU
module ALU (
  input  [31:0] X,
  input  [31:0] Y,
  input  [3:0] AluOP,
  output Signed_Overflow,
  output UnSigned_Overflow,
  output Equal,
  output [31:0] Result,
  output [31:0] Result_2
);

  wire comparator_1_lt, comparator_2_lt, \n32bit_1_cout有符号溢出 , \n32bit_1_cout溢出 , \n32bit_2_cout有符号溢出 ,
       \n32bit_2_cout溢出 , not_2_out;
  wire [4:0] bitselector_1_out;
  wire [31:0] and_1_out, bit_extender_1_out, bit_extender_2_out, divider_1_out, divider_1_rem,
       multiplier_1_cout, multiplier_1_out, n32bit_1_s, n32bit_2_s, nor_1_out, not_1_out, or_1_out,
       shifter_1_out, shifter_2_out, shifter_3_out, xor_1_out;

  // Probe on X
  // Probe on X
  // Probe on Y
  // Probe on Y
  BitSelector #(.width(32), .group(5)) bitselector_1 (.in(Y), .out(bitselector_1_out), .sel(3'b000));
  assign not_1_out = ~Y;  // NOT_Gate not_1, 32 bits wide
  Shifter #(.width(32)) shifter_1 (.in(X), .\dist (bitselector_1_out), .out(shifter_1_out));
  Shifter #(.width(32), .shift("ar")) shifter_2 (.in(X), .\dist (bitselector_1_out), .out(shifter_2_out));
  Shifter #(.width(32), .shift("lr")) shifter_3 (.in(X), .\dist (bitselector_1_out), .out(shifter_3_out));
  Multiplier #(.width(32)) multiplier_1 (
    .a(X), .b(Y), .out(multiplier_1_out), .cin({32{1'b0}}), .cout(multiplier_1_cout));
  Divider #(.width(32)) divider_1 (.a(X), .b(Y), .out(divider_1_out), .upper({32{1'b0}}), .rem(divider_1_rem));
  _32BIT u_32bit_1 (
    .y(Y), .x(X), .S(n32bit_1_s), .\Cout溢出 (\n32bit_1_cout溢出 ), .\Cout有符号溢出 (\n32bit_1_cout有符号溢出 ), .Cin(1'b0));
  _32BIT u_32bit_2 (
    .y(not_1_out), .x(X), .S(n32bit_2_s), .\Cout溢出 (\n32bit_2_cout溢出 ), .\Cout有符号溢出 (\n32bit_2_cout有符号溢出 ),
    .Cin(1'b1));
  assign and_1_out = X & Y;  // AND_Gate and_1, 32 bits wide
  assign or_1_out = X | Y;  // OR_Gate or_1, 32 bits wide
  assign xor_1_out = X ^ Y;  // XOR_Gate xor_1, 32 bits wide
  assign nor_1_out = ~(X | Y);  // NOR_Gate nor_1, 32 bits wide
  Comparator #(.width(32)) comparator_1 (.a(X), .b(Y), .lt(comparator_1_lt));  // open: gt, eq
  Comparator #(.width(32), .mode("unsigned")) comparator_2 (
    .a(X), .b(Y), .eq(Equal), .lt(comparator_2_lt));  // open: gt
  // Probe on AluOP
  assign bit_extender_1_out = {{31{1'b0}}, comparator_1_lt};  // Bit_Extender bit_extender_1
  assign bit_extender_2_out = {{31{1'b0}}, comparator_2_lt};  // Bit_Extender bit_extender_2
  // Probe on Result
  // Probe on Result
  // Probe on Result_2
  not not_2 (not_2_out, \n32bit_2_cout溢出 );
  Multiplexer #(.select(4), .width(32)) multiplexer_1 (
    .in0(shifter_1_out), .in1(shifter_2_out), .in2(shifter_3_out), .in3(multiplier_1_out),
    .in4(divider_1_out), .in5(n32bit_1_s), .in6(n32bit_2_s), .in7(and_1_out), .in8(or_1_out),
    .in9(xor_1_out), .in10(nor_1_out), .in11(bit_extender_1_out), .in12(bit_extender_2_out),
    .in13({32{1'b0}}), .in14({32{1'b0}}), .in15({32{1'b0}}), .out(Result), .sel(AluOP), .en(1'b1));
  Multiplexer #(.select(4), .width(32)) multiplexer_2 (
    .in0({32{1'b0}}), .in1({32{1'b0}}), .in2({32{1'b0}}), .in3(multiplier_1_cout), .in4(divider_1_rem),
    .in5({32{1'b0}}), .in6({32{1'b0}}), .in7({32{1'b0}}), .in8({32{1'b0}}), .in9({32{1'b0}}),
    .in10({32{1'b0}}), .in11({32{1'b0}}), .in12({32{1'b0}}), .in13({32{1'b0}}), .in14({32{1'b0}}),
    .in15({32{1'b0}}), .out(Result_2), .sel(AluOP), .en(1'b1));
  Multiplexer #(.select(4)) multiplexer_3 (
    .in0(1'b0), .in1(1'b0), .in2(1'b0), .in3(1'b0), .in4(1'b0), .in5(\n32bit_1_cout有符号溢出 ),
    .in6(\n32bit_2_cout有符号溢出 ), .in7(1'b0), .in8(1'b0), .in9(1'b0), .in10(1'b0), .in11(1'b0), .in12(1'b0),
    .in13(1'b0), .in14(1'b0), .in15(1'b0), .out(Signed_Overflow), .sel(AluOP), .en(1'b1));
  Multiplexer #(.select(4)) multiplexer_4 (
    .in0(1'b0), .in1(1'b0), .in2(1'b0), .in3(1'b0), .in4(1'b0), .in5(\n32bit_1_cout溢出 ), .in6(not_2_out),
    .in7(1'b0), .in8(1'b0), .in9(1'b0), .in10(1'b0), .in11(1'b0), .in12(1'b0), .in13(1'b0), .in14(1'b0),
    .in15(1'b0), .out(UnSigned_Overflow), .sel(AluOP), .en(1'b1));

  // Other names for the same wires on the sheet: OF = Signed_Overflow; Result2[31:0] = Result_2; S[3:0] = AluOP;
  //   UOF = UnSigned_Overflow

  // Notes on the sheet:
  //   不要改变此引脚区域内容，也不要改变ALU封装形式
  //   输入引脚
  //   请在下方利用上方输入输出引脚的隧道信号构建ALU电路，ctrl+d复制选择部件
  //   华中科技大学计算机学院 计算机组成原理，鸣谢加州大学伯克利CS61C课程
  //   输出引脚
  //   探测区域
endmodule

module \演示电路  (
  input  [31:0] X,
  input  [31:0] Y,
  input  [3:0] ALUOP,
  output Signed_Overflow,
  output Unsigned_overflow,
  output [31:0] Result,
  output [31:0] Result_2,
  output Equal
);

  // Probe on X
  // Probe on X
  ALU alu_1 (
    .AluOP(ALUOP), .X(X), .Equal(Equal), .Result(Result), .Signed_Overflow(Signed_Overflow), .Y(Y),
    .Result_2(Result_2), .UnSigned_Overflow(Unsigned_overflow));
  // Probe on ALUOP
  // Probe on Y
  // Probe on Y
  // Probe on Result
  // Probe on Result
  // Probe on Result_2

  // Notes on the sheet:
  //   ALu电路无需调整位置即可连接在该电路中，并且不能出现蓝色线缆和三态输出
endmodule

module \等差数列  (
  input  [31:0] \数列初始值 ,
  input  [31:0] \等差值 ,
  input  \时钟 ,
  output [31:0] Result
);

  // Probe on \数列初始值 
  // Probe on \数列初始值 
  // Probe on \等差值 
  // Probe on \等差值 
  // Probe on Result
  // Probe on Result

  // Other names for the same wires on the sheet: 数列初值[31:0] = \数列初始值 ; 累加和[31:0] = Result

  // Notes on the sheet:
  //   不要改变此引脚区域内容，也不要改变ALU封装形式
  //   请在下方利用上方输入输出引脚的隧道信号构建等差数列求和电路，ctrl+d复制选择部件
  //   华中科技大学计算机学院 计算机组成原理，鸣谢加州大学伯克利CS61C课程
  //   输出引脚
  //   探测区域
endmodule

module _4bits_74182 (
  input  in_1,
  input  [3:0] G,
  input  [3:0] p,
  output G4_star,
  output [3:0] C1,
  output P4_star
);

  wire and_1_out, and_2_out, and_3_out, and_4_out, and_5_out, and_6_out, and_7_out, and_8_out, and_9_out,
       and_10_out, and_11_out, and_12_out, and_13_out;

  and and_1 (and_1_out, p[3], G[2]);
  or or_1 (C1[3], G[3], and_1_out, and_2_out, and_4_out, and_6_out);
  and and_2 (and_2_out, p[3], p[2], G[1]);
  and and_3 (and_3_out, p[3], G[2]);
  and and_4 (and_4_out, p[3], p[2], p[1], G[0]);
  or or_2 (G4_star, and_3_out, and_5_out, G[3], and_7_out);
  and and_5 (and_5_out, p[3], p[2], G[1]);
  and and_6 (and_6_out, p[3], p[2], p[1], p[0], in_1);
  and and_7 (and_7_out, p[3], p[2], p[1], G[0]);
  or or_3 (C1[2], G[2], and_8_out, and_9_out, and_10_out);
  and and_8 (and_8_out, p[2], G[1]);
  and and_9 (and_9_out, p[2], p[1], G[0]);
  and and_10 (and_10_out, p[2], p[1], p[0], in_1);
  or or_4 (C1[1], G[1], and_11_out, and_12_out);
  and and_11 (and_11_out, p[1], G[0]);
  and and_12 (and_12_out, p[1], p[0], in_1);
  or or_5 (C1[0], G[0], and_13_out);
  and and_13 (and_13_out, p[0], in_1);
  and and_14 (P4_star, p[0], p[1], p[2], p[3]);

  // Notes on the sheet:
  //   C0
endmodule

module GP (
  input  [3:0] X,
  input  [3:0] Y,
  output [3:0] Gout,
  output [3:0] Pout
);

  and and_1 (Gout[3], X[3], Y[3]);
  xor xor_1 (Pout[3], Y[3], X[3]);
  and and_2 (Gout[2], X[2], Y[2]);
  xor xor_2 (Pout[2], Y[2], X[2]);
  and and_3 (Gout[1], X[1], Y[1]);
  xor xor_3 (Pout[1], Y[1], X[1]);
  and and_4 (Gout[0], X[0], Y[0]);
  xor xor_4 (Pout[0], Y[0], X[0]);
endmodule

module _4_add_74181 (
  input  C0,
  input  [3:0] y,
  input  [3:0] x,
  output [3:0] S,
  output out,
  output C4out,
  output G_star,
  output P_star
);

  wire [1:0] n4bits_74182_1_c1;
  wire [3:0] gp_1_gout, gp_1_pout;

  xor xor_1 (S[3], gp_1_pout[3], out);
  xor xor_2 (S[2], n4bits_74182_1_c1[1], gp_1_pout[2]);
  GP gp_1 (.Gout(gp_1_gout), .Pout(gp_1_pout), .X(x), .Y(y));
  _4bits_74182 u_4bits_74182_1 (
    .G4_star(G_star), .C1({C4out, out, n4bits_74182_1_c1}), .P4_star(P_star), .in_1(C0), .p(gp_1_pout),
    .G(gp_1_gout));
  xor xor_3 (S[1], n4bits_74182_1_c1[0], gp_1_pout[1]);
  xor xor_4 (S[0], gp_1_pout[0], C0);
endmodule

module _32BIT (
  input  Cin,
  input  [31:0] x,
  input  [31:0] y,
  output \Cout有符号溢出 ,
  output \Cout溢出 ,
  output [31:0] S
);

  wire n4_add_74181_1_out;
  wire [1:0] n4bits_74182_3_g4_star, n4bits_74182_3_p4_star;
  wire [2:0] n4_add_74181_4_c4out;
  wire [3:0] n4_add_74181_4_p_star, n4_add_74181_8_c4out, n4_add_74181_8_p_star, n4bits_74182_1_c1,
       n4bits_74182_2_c1, n4bits_74182_3_c1;

  xor xor_1 (\Cout有符号溢出 , n4_add_74181_1_out, \Cout溢出 );
  _4_add_74181 u_4_add_74181_1 (
    .S(S[31:28]), .C4out(\Cout溢出 ), .P_star(n4_add_74181_4_p_star[3]), .C0(n4bits_74182_1_c1[2]),
    .y(x[31:28]), .x(y[31:28]), .out(n4_add_74181_1_out));  // open: G_star
  _4_add_74181 u_4_add_74181_2 (
    .S(S[27:24]), .C4out(n4_add_74181_4_c4out[2]), .P_star(n4_add_74181_4_p_star[2]),
    .C0(n4bits_74182_1_c1[1]), .y(x[27:24]), .x(y[27:24]));  // open: G_star, out
  _4bits_74182 u_4bits_74182_1 (
    .G4_star(n4bits_74182_3_g4_star[1]), .C1(n4bits_74182_1_c1), .P4_star(n4bits_74182_3_p4_star[1]),
    .in_1(n4bits_74182_2_c1[0]), .p(n4_add_74181_4_p_star), .G({\Cout溢出 , n4_add_74181_4_c4out}));
  _4_add_74181 u_4_add_74181_3 (
    .S(S[23:20]), .C4out(n4_add_74181_4_c4out[1]), .P_star(n4_add_74181_4_p_star[1]),
    .C0(n4bits_74182_1_c1[0]), .y(x[23:20]), .x(y[23:20]));  // open: G_star, out
  _4bits_74182 u_4bits_74182_2 (
    .C1(n4bits_74182_2_c1), .in_1(Cin), .p({2'b00, n4bits_74182_3_p4_star}),
    .G({2'b00, n4bits_74182_3_g4_star}));  // open: G4_star, P4_star
  _4_add_74181 u_4_add_74181_4 (
    .S(S[19:16]), .C4out(n4_add_74181_4_c4out[0]), .P_star(n4_add_74181_4_p_star[0]),
    .C0(n4bits_74182_2_c1[0]), .y(x[19:16]), .x(y[19:16]));  // open: G_star, out
  _4_add_74181 u_4_add_74181_5 (
    .S(S[15:12]), .C4out(n4_add_74181_8_c4out[3]), .P_star(n4_add_74181_8_p_star[3]),
    .C0(n4bits_74182_3_c1[2]), .y(x[15:12]), .x(y[15:12]));  // open: G_star, out
  _4_add_74181 u_4_add_74181_6 (
    .S(S[11:8]), .C4out(n4_add_74181_8_c4out[2]), .P_star(n4_add_74181_8_p_star[2]),
    .C0(n4bits_74182_3_c1[1]), .y(x[11:8]), .x(y[11:8]));  // open: G_star, out
  _4bits_74182 u_4bits_74182_3 (
    .G4_star(n4bits_74182_3_g4_star[0]), .C1(n4bits_74182_3_c1), .P4_star(n4bits_74182_3_p4_star[0]),
    .in_1(Cin), .p(n4_add_74181_8_p_star), .G(n4_add_74181_8_c4out));
  _4_add_74181 u_4_add_74181_7 (
    .S(S[7:4]), .C4out(n4_add_74181_8_c4out[1]), .P_star(n4_add_74181_8_p_star[1]),
    .C0(n4bits_74182_3_c1[0]), .y(x[7:4]), .x(y[7:4]));  // open: G_star, out
  _4_add_74181 u_4_add_74181_8 (
    .S(S[3:0]), .C4out(n4_add_74181_8_c4out[0]), .P_star(n4_add_74181_8_p_star[0]), .C0(Cin), .y(x[3:0]),
    .x(y[3:0]));  // open: G_star, out
endmodule
