// Logisim project CS1409_U201414803_许荣仁_mipscpu.circ as structural Verilog: 6 circuits, main circuit main
module decoder1 (
  input  o0,
  input  o1,
  input  o2,
  input  o3,
  input  o4,
  input  o5,
  input  f0,
  input  f1,
  input  f2,
  input  f3,
  input  f4,
  input  f5,
  output add,
  output addi,
  output addiu,
  output addu,
  output \and ,
  output andi,
  output sll,
  output sra,
  output srl,
  output sub,
  output \or ,
  output ori
);

  wire not_1_out, not_2_out, not_3_out, not_4_out, not_5_out, not_6_out, not_7_out, not_8_out, not_9_out,
       not_10_out, not_11_out, not_12_out, not_13_out, not_14_out, not_15_out, not_16_out, not_17_out,
       not_18_out, not_19_out, not_20_out, not_21_out, not_22_out, not_23_out, not_24_out, not_25_out,
       not_26_out, not_27_out, not_28_out, not_29_out, not_30_out, not_31_out, not_32_out, not_33_out,
       not_34_out, not_35_out, not_36_out, not_37_out, not_38_out, not_39_out, not_40_out, not_41_out,
       not_42_out, not_43_out, not_44_out, not_45_out, not_46_out, not_47_out, not_48_out, not_49_out,
       not_50_out, not_51_out, not_52_out, not_53_out, not_54_out, not_55_out, not_56_out, not_57_out,
       not_58_out, not_59_out, not_60_out, not_61_out, not_62_out, not_63_out, not_64_out, not_65_out,
       not_66_out, not_67_out, not_68_out, not_69_out, not_70_out, not_71_out, not_72_out, not_73_out,
       not_74_out, not_75_out, not_76_out, not_77_out, not_78_out, not_79_out, not_80_out, not_81_out,
       not_82_out, not_83_out, not_84_out, not_85_out, not_86_out, not_87_out, not_88_out, not_89_out,
       not_90_out, not_91_out, not_92_out, not_93_out, not_94_out, not_95_out, not_96_out, not_97_out,
       not_98_out, not_99_out;

  not not_1 (not_1_out, o0);
  not not_2 (not_2_out, o1);
  not not_3 (not_3_out, o2);
  not not_4 (not_4_out, o3);
  not not_5 (not_5_out, o4);
  not not_6 (not_6_out, o5);
  not not_7 (not_7_out, f1);
  not not_8 (not_8_out, f2);
  not not_9 (not_9_out, f3);
  not not_10 (not_10_out, f4);
  not not_11 (not_11_out, f5);
  not not_12 (not_12_out, o0);
  not not_13 (not_13_out, o1);
  not not_14 (not_14_out, o3);
  not not_15 (not_15_out, o4);
  not not_16 (not_16_out, o5);
  not not_17 (not_17_out, o0);
  not not_18 (not_18_out, o1);
  not not_19 (not_19_out, o3);
  not not_20 (not_20_out, o4);
  not not_21 (not_21_out, o0);
  not not_22 (not_22_out, o1);
  not not_23 (not_23_out, o2);
  not not_24 (not_24_out, o3);
  not not_25 (not_25_out, o4);
  not not_26 (not_26_out, o5);
  not not_27 (not_27_out, f1);
  not not_28 (not_28_out, f2);
  not not_29 (not_29_out, f3);
  not not_30 (not_30_out, f4);
  not not_31 (not_31_out, o0);
  not not_32 (not_32_out, o1);
  not not_33 (not_33_out, o2);
  not not_34 (not_34_out, o3);
  not not_35 (not_35_out, o4);
  not not_36 (not_36_out, o5);
  not not_37 (not_37_out, f1);
  not not_38 (not_38_out, f2);
  not not_39 (not_39_out, f4);
  not not_40 (not_40_out, f5);
  not not_41 (not_41_out, o0);
  not not_42 (not_42_out, o1);
  not not_43 (not_43_out, o4);
  not not_44 (not_44_out, o5);
  not not_45 (not_45_out, o0);
  not not_46 (not_46_out, o1);
  not not_47 (not_47_out, o2);
  not not_48 (not_48_out, o3);
  not not_49 (not_49_out, o4);
  not not_50 (not_50_out, o5);
  not not_51 (not_51_out, f0);
  not not_52 (not_52_out, f1);
  not not_53 (not_53_out, f2);
  not not_54 (not_54_out, f3);
  not not_55 (not_55_out, f4);
  not not_56 (not_56_out, f5);
  not not_57 (not_57_out, o0);
  not not_58 (not_58_out, o1);
  not not_59 (not_59_out, o2);
  not not_60 (not_60_out, o3);
  not not_61 (not_61_out, o4);
  not not_62 (not_62_out, o5);
  not not_63 (not_63_out, f0);
  not not_64 (not_64_out, f1);
  not not_65 (not_65_out, f2);
  not not_66 (not_66_out, f3);
  not not_67 (not_67_out, o0);
  not not_68 (not_68_out, o1);
  not not_69 (not_69_out, o2);
  not not_70 (not_70_out, o3);
  not not_71 (not_71_out, o4);
  not not_72 (not_72_out, o5);
  not not_73 (not_73_out, f0);
  not not_74 (not_74_out, f1);
  not not_75 (not_75_out, f2);
  not not_76 (not_76_out, f3);
  not not_77 (not_77_out, f5);
  not not_78 (not_78_out, o0);
  not not_79 (not_79_out, o1);
  not not_80 (not_80_out, o2);
  not not_81 (not_81_out, o3);
  not not_82 (not_82_out, o4);
  not not_83 (not_83_out, o5);
  not not_84 (not_84_out, f1);
  not not_85 (not_85_out, f2);
  not not_86 (not_86_out, f3);
  not not_87 (not_87_out, f5);
  not not_88 (not_88_out, o0);
  not not_89 (not_89_out, o1);
  not not_90 (not_90_out, o2);
  not not_91 (not_91_out, o3);
  not not_92 (not_92_out, o4);
  not not_93 (not_93_out, o5);
  not not_94 (not_94_out, f1);
  not not_95 (not_95_out, f2);
  not not_96 (not_96_out, f4);
  not not_97 (not_97_out, o0);
  not not_98 (not_98_out, o1);
  not not_99 (not_99_out, o4);
  and and_1 (add, not_1_out, not_2_out, not_3_out, not_4_out, not_5_out, not_6_out, f0, not_7_out, not_8_out, not_9_out, not_10_out, not_11_out);
  and and_2 (addi, not_12_out, not_13_out, o2, not_14_out, not_15_out, not_16_out);
  and and_3 (addiu, not_17_out, not_18_out, o2, not_19_out, not_20_out, o5);
  and and_4 (addu, not_21_out, not_22_out, not_23_out, not_24_out, not_25_out, not_26_out, f0, not_27_out, not_28_out, not_29_out, not_30_out, f5);
  and and_5 (\and , not_31_out, not_32_out, not_33_out, not_34_out, not_35_out, not_36_out, f0, not_37_out, not_38_out, f3, not_39_out, not_40_out);
  and and_6 (andi, not_41_out, not_42_out, o2, o3, not_43_out, not_44_out);
  and and_7 (sll, not_45_out, not_46_out, not_47_out, not_48_out, not_49_out, not_50_out, not_51_out, not_52_out, not_53_out, not_54_out, not_55_out, not_56_out);
  and and_8 (sra, not_57_out, not_58_out, not_59_out, not_60_out, not_61_out, not_62_out, not_63_out, not_64_out, not_65_out, not_66_out, f4, f5);
  and and_9 (srl, not_67_out, not_68_out, not_69_out, not_70_out, not_71_out, not_72_out, not_73_out, not_74_out, not_75_out, not_76_out, f4, not_77_out);
  and and_10 (sub, not_78_out, not_79_out, not_80_out, not_81_out, not_82_out, not_83_out, f0, not_84_out, not_85_out, not_86_out, f4, not_87_out);
  and and_11 (\or , not_88_out, not_89_out, not_90_out, not_91_out, not_92_out, not_93_out, f0, not_94_out, not_95_out, f3, not_96_out, f5);
  and and_12 (ori, not_97_out, not_98_out, o2, o3, not_99_out, o5);
endmodule

module decoder2 (
  input  o0,
  input  o1,
  input  o2,
  input  o3,
  input  o4,
  input  o5,
  input  f0,
  input  f1,
  input  f2,
  input  f3,
  input  f4,
  input  f5,
  output \nor ,
  output lw,
  output sw,
  output beq,
  output bne,
  output slt,
  output slti,
  output sltu,
  output jump,
  output jmpl,
  output jmpr,
  output syscall
);

  wire not_1_out, not_2_out, not_3_out, not_4_out, not_5_out, not_6_out, not_7_out, not_8_out, not_9_out,
       not_10_out, not_11_out, not_12_out, not_13_out, not_14_out, not_15_out, not_16_out, not_17_out,
       not_18_out, not_19_out, not_20_out, not_21_out, not_22_out, not_23_out, not_24_out, not_25_out,
       not_26_out, not_27_out, not_28_out, not_29_out, not_30_out, not_31_out, not_32_out, not_33_out,
       not_34_out, not_35_out, not_36_out, not_37_out, not_38_out, not_39_out, not_40_out, not_41_out,
       not_42_out, not_43_out, not_44_out, not_45_out, not_46_out, not_47_out, not_48_out, not_49_out,
       not_50_out, not_51_out, not_52_out, not_53_out, not_54_out, not_55_out, not_56_out, not_57_out,
       not_58_out, not_59_out, not_60_out, not_61_out, not_62_out, not_63_out, not_64_out, not_65_out,
       not_66_out, not_67_out, not_68_out, not_69_out, not_70_out, not_71_out, not_72_out, not_73_out;

  not not_1 (not_1_out, o0);
  not not_2 (not_2_out, o1);
  not not_3 (not_3_out, o2);
  not not_4 (not_4_out, o3);
  not not_5 (not_5_out, o4);
  not not_6 (not_6_out, o5);
  not not_7 (not_7_out, f1);
  not not_8 (not_8_out, f2);
  not not_9 (not_9_out, o1);
  not not_10 (not_10_out, o2);
  not not_11 (not_11_out, o3);
  not not_12 (not_12_out, o1);
  not not_13 (not_13_out, o3);
  not not_14 (not_14_out, o0);
  not not_15 (not_15_out, o1);
  not not_16 (not_16_out, o2);
  not not_17 (not_17_out, o4);
  not not_18 (not_18_out, o5);
  not not_19 (not_19_out, o0);
  not not_20 (not_20_out, o1);
  not not_21 (not_21_out, o2);
  not not_22 (not_22_out, o4);
  not not_23 (not_23_out, o0);
  not not_24 (not_24_out, o1);
  not not_25 (not_25_out, o2);
  not not_26 (not_26_out, o3);
  not not_27 (not_27_out, o4);
  not not_28 (not_28_out, o5);
  not not_29 (not_29_out, f1);
  not not_30 (not_30_out, f3);
  not not_31 (not_31_out, f5);
  not not_32 (not_32_out, o0);
  not not_33 (not_33_out, o1);
  not not_34 (not_34_out, o3);
  not not_35 (not_35_out, o5);
  not not_36 (not_36_out, o0);
  not not_37 (not_37_out, o1);
  not not_38 (not_38_out, o2);
  not not_39 (not_39_out, o3);
  not not_40 (not_40_out, o4);
  not not_41 (not_41_out, o5);
  not not_42 (not_42_out, f1);
  not not_43 (not_43_out, f3);
  not not_44 (not_44_out, o0);
  not not_45 (not_45_out, o1);
  not not_46 (not_46_out, o2);
  not not_47 (not_47_out, o3);
  not not_48 (not_48_out, o5);
  not not_49 (not_49_out, o0);
  not not_50 (not_50_out, o1);
  not not_51 (not_51_out, o2);
  not not_52 (not_52_out, o3);
  not not_53 (not_53_out, o0);
  not not_54 (not_54_out, o1);
  not not_55 (not_55_out, o2);
  not not_56 (not_56_out, o3);
  not not_57 (not_57_out, o4);
  not not_58 (not_58_out, o5);
  not not_59 (not_59_out, f0);
  not not_60 (not_60_out, f1);
  not not_61 (not_61_out, f3);
  not not_62 (not_62_out, f4);
  not not_63 (not_63_out, f5);
  not not_64 (not_64_out, o0);
  not not_65 (not_65_out, o1);
  not not_66 (not_66_out, o2);
  not not_67 (not_67_out, o3);
  not not_68 (not_68_out, o4);
  not not_69 (not_69_out, o5);
  not not_70 (not_70_out, f0);
  not not_71 (not_71_out, f1);
  not not_72 (not_72_out, f4);
  not not_73 (not_73_out, f5);
  and and_1 (\nor , not_1_out, not_2_out, not_3_out, not_4_out, not_5_out, not_6_out, f0, not_7_out, not_8_out, f3, f4, f5);
  and and_2 (lw, o0, not_9_out, not_10_out, not_11_out, o4, o5);
  and and_3 (sw, o0, not_12_out, o2, not_13_out, o4, o5);
  and and_4 (beq, not_14_out, not_15_out, not_16_out, o3, not_17_out, not_18_out);
  and and_5 (bne, not_19_out, not_20_out, not_21_out, o3, not_22_out, o5);
  and and_6 (slt, not_23_out, not_24_out, not_25_out, not_26_out, not_27_out, not_28_out, f0, not_29_out, f2, not_30_out, f4, not_31_out);
  and and_7 (slti, not_32_out, not_33_out, o2, not_34_out, o4, not_35_out);
  and and_8 (sltu, not_36_out, not_37_out, not_38_out, not_39_out, not_40_out, not_41_out, f0, not_42_out, f2, not_43_out, f4, f5);
  and and_9 (jump, not_44_out, not_45_out, not_46_out, not_47_out, o4, not_48_out);
  and and_10 (jmpl, not_49_out, not_50_out, not_51_out, not_52_out, o4, o5);
  and and_11 (jmpr, not_53_out, not_54_out, not_55_out, not_56_out, not_57_out, not_58_out, not_59_out, not_60_out, f2, not_61_out, not_62_out, not_63_out);
  and and_12 (syscall, not_64_out, not_65_out, not_66_out, not_67_out, not_68_out, not_69_out, not_70_out, not_71_out, f2, f3, not_72_out, not_73_out);
endmodule

module decoderrr (
  input  o0,
  input  o1,
  input  o2,
  input  o3,
  input  o4,
  input  o5,
  input  f0,
  input  f1,
  input  f2,
  input  f3,
  input  f4,
  input  f5,
  output add,
  output \nor ,
  output lw,
  output addi,
  output sw,
  output addiu,
  output beq,
  output bne,
  output addu,
  output slt,
  output \and ,
  output slti,
  output andi,
  output sltu,
  output sll,
  output jump,
  output jmpl,
  output sra,
  output jmpr,
  output srl,
  output syscall,
  output sub,
  output \or ,
  output ori
);

  wire not_1_out, not_2_out, not_3_out, not_4_out, not_5_out, not_6_out, not_7_out, not_8_out, not_9_out,
       not_10_out, not_11_out, not_12_out, not_13_out, not_14_out, not_15_out, not_16_out, not_17_out,
       not_18_out, not_19_out, not_20_out, not_21_out, not_22_out, not_23_out, not_24_out, not_25_out,
       not_26_out, not_27_out, not_28_out, not_29_out, not_30_out, not_31_out, not_32_out, not_33_out,
       not_34_out, not_35_out, not_36_out, not_37_out, not_38_out, not_39_out, not_40_out, not_41_out,
       not_42_out, not_43_out, not_44_out, not_45_out, not_46_out, not_47_out, not_48_out, not_49_out,
       not_50_out, not_51_out, not_52_out, not_53_out, not_54_out, not_55_out, not_56_out, not_57_out,
       not_58_out, not_59_out, not_60_out, not_61_out, not_62_out, not_63_out, not_64_out, not_65_out,
       not_66_out, not_67_out, not_68_out, not_69_out, not_70_out, not_71_out, not_72_out, not_73_out,
       not_74_out, not_75_out, not_76_out, not_77_out, not_78_out, not_79_out, not_80_out, not_81_out,
       not_82_out, not_83_out, not_84_out, not_85_out, not_86_out, not_87_out, not_88_out, not_89_out,
       not_90_out, not_91_out, not_92_out, not_93_out, not_94_out, not_95_out, not_96_out, not_97_out,
       not_98_out, not_99_out, not_100_out, not_101_out, not_102_out, not_103_out, not_104_out, not_105_out,
       not_106_out, not_107_out, not_108_out, not_109_out, not_110_out, not_111_out, not_112_out,
       not_113_out, not_114_out, not_115_out, not_116_out, not_117_out, not_118_out, not_119_out,
       not_120_out, not_121_out, not_122_out, not_123_out, not_124_out, not_125_out, not_126_out,
       not_127_out, not_128_out, not_129_out, not_130_out, not_131_out, not_132_out, not_133_out,
       not_134_out, not_135_out, not_136_out, not_137_out, not_138_out, not_139_out, not_140_out,
       not_141_out, not_142_out, not_143_out, not_144_out, not_145_out, not_146_out, not_147_out,
       not_148_out, not_149_out, not_150_out, not_151_out, not_152_out, not_153_out, not_154_out,
       not_155_out, not_156_out, not_157_out, not_158_out, not_159_out, not_160_out, not_161_out,
       not_162_out, not_163_out, not_164_out, not_165_out, not_166_out, not_167_out, not_168_out,
       not_169_out, not_170_out, not_171_out, not_172_out;

  not not_1 (not_1_out, o0);
  not not_2 (not_2_out, o1);
  not not_3 (not_3_out, o2);
  not not_4 (not_4_out, o3);
  not not_5 (not_5_out, o4);
  not not_6 (not_6_out, o5);
  not not_7 (not_7_out, f1);
  not not_8 (not_8_out, f2);
  not not_9 (not_9_out, f3);
  not not_10 (not_10_out, f4);
  not not_11 (not_11_out, f5);
  not not_12 (not_12_out, o0);
  not not_13 (not_13_out, o1);
  not not_14 (not_14_out, o3);
  not not_15 (not_15_out, o4);
  not not_16 (not_16_out, o5);
  not not_17 (not_17_out, o0);
  not not_18 (not_18_out, o1);
  not not_19 (not_19_out, o3);
  not not_20 (not_20_out, o4);
  not not_21 (not_21_out, o0);
  not not_22 (not_22_out, o1);
  not not_23 (not_23_out, o2);
  not not_24 (not_24_out, o3);
  not not_25 (not_25_out, o4);
  not not_26 (not_26_out, o5);
  not not_27 (not_27_out, f1);
  not not_28 (not_28_out, f2);
  not not_29 (not_29_out, f3);
  not not_30 (not_30_out, f4);
  not not_31 (not_31_out, o0);
  not not_32 (not_32_out, o1);
  not not_33 (not_33_out, o2);
  not not_34 (not_34_out, o3);
  not not_35 (not_35_out, o4);
  not not_36 (not_36_out, o5);
  not not_37 (not_37_out, f1);
  not not_38 (not_38_out, f2);
  not not_39 (not_39_out, f4);
  not not_40 (not_40_out, f5);
  not not_41 (not_41_out, o0);
  not not_42 (not_42_out, o1);
  not not_43 (not_43_out, o4);
  not not_44 (not_44_out, o5);
  not not_45 (not_45_out, o0);
  not not_46 (not_46_out, o1);
  not not_47 (not_47_out, o2);
  not not_48 (not_48_out, o3);
  not not_49 (not_49_out, o4);
  not not_50 (not_50_out, o5);
  not not_51 (not_51_out, f0);
  not not_52 (not_52_out, f1);
  not not_53 (not_53_out, f2);
  not not_54 (not_54_out, f3);
  not not_55 (not_55_out, f4);
  not not_56 (not_56_out, f5);
  not not_57 (not_57_out, o0);
  not not_58 (not_58_out, o1);
  not not_59 (not_59_out, o2);
  not not_60 (not_60_out, o3);
  not not_61 (not_61_out, o4);
  not not_62 (not_62_out, o5);
  not not_63 (not_63_out, f0);
  not not_64 (not_64_out, f1);
  not not_65 (not_65_out, f2);
  not not_66 (not_66_out, f3);
  not not_67 (not_67_out, o0);
  not not_68 (not_68_out, o1);
  not not_69 (not_69_out, o2);
  not not_70 (not_70_out, o3);
  not not_71 (not_71_out, o4);
  not not_72 (not_72_out, o5);
  not not_73 (not_73_out, f0);
  not not_74 (not_74_out, f1);
  not not_75 (not_75_out, f2);
  not not_76 (not_76_out, f3);
  not not_77 (not_77_out, f5);
  not not_78 (not_78_out, o0);
  not not_79 (not_79_out, o1);
  not not_80 (not_80_out, o2);
  not not_81 (not_81_out, o3);
  not not_82 (not_82_out, o4);
  not not_83 (not_83_out, o5);
  not not_84 (not_84_out, f1);
  not not_85 (not_85_out, f2);
  not not_86 (not_86_out, f3);
  not not_87 (not_87_out, f5);
  not not_88 (not_88_out, o0);
  not not_89 (not_89_out, o1);
  not not_90 (not_90_out, o2);
  not not_91 (not_91_out, o3);
  not not_92 (not_92_out, o4);
  not not_93 (not_93_out, o5);
  not not_94 (not_94_out, f1);
  not not_95 (not_95_out, f2);
  not not_96 (not_96_out, f4);
  not not_97 (not_97_out, o0);
  not not_98 (not_98_out, o1);
  not not_99 (not_99_out, o4);
  and and_1 (addi, not_12_out, not_13_out, o2, not_14_out, not_15_out, not_16_out);
  and and_2 (addiu, not_17_out, not_18_out, o2, not_19_out, not_20_out, o5);
  and and_3 (andi, not_41_out, not_42_out, o2, o3, not_43_out, not_44_out);
  and and_4 (ori, not_97_out, not_98_out, o2, o3, not_99_out, o5);
  and and_5 (add, not_1_out, not_2_out, not_3_out, not_4_out, not_5_out, not_6_out, f0, not_7_out, not_8_out, not_9_out, not_10_out, not_11_out);
  and and_6 (addu, not_21_out, not_22_out, not_23_out, not_24_out, not_25_out, not_26_out, f0, not_27_out, not_28_out, not_29_out, not_30_out, f5);
  and and_7 (\and , not_31_out, not_32_out, not_33_out, not_34_out, not_35_out, not_36_out, f0, not_37_out, not_38_out, f3, not_39_out, not_40_out);
  and and_8 (sll, not_45_out, not_46_out, not_47_out, not_48_out, not_49_out, not_50_out, not_51_out, not_52_out, not_53_out, not_54_out, not_55_out, not_56_out);
  and and_9 (sra, not_57_out, not_58_out, not_59_out, not_60_out, not_61_out, not_62_out, not_63_out, not_64_out, not_65_out, not_66_out, f4, f5);
  and and_10 (srl, not_67_out, not_68_out, not_69_out, not_70_out, not_71_out, not_72_out, not_73_out, not_74_out, not_75_out, not_76_out, f4, not_77_out);
  and and_11 (sub, not_78_out, not_79_out, not_80_out, not_81_out, not_82_out, not_83_out, f0, not_84_out, not_85_out, not_86_out, f4, not_87_out);
  and and_12 (\or , not_88_out, not_89_out, not_90_out, not_91_out, not_92_out, not_93_out, f0, not_94_out, not_95_out, f3, not_96_out, f5);
  not not_100 (not_100_out, o0);
  not not_101 (not_101_out, o1);
  not not_102 (not_102_out, o2);
  not not_103 (not_103_out, o3);
  not not_104 (not_104_out, o4);
  not not_105 (not_105_out, o5);
  not not_106 (not_106_out, f1);
  not not_107 (not_107_out, f2);
  not not_108 (not_108_out, o1);
  not not_109 (not_109_out, o2);
  not not_110 (not_110_out, o3);
  not not_111 (not_111_out, o1);
  not not_112 (not_112_out, o3);
  not not_113 (not_113_out, o0);
  not not_114 (not_114_out, o1);
  not not_115 (not_115_out, o2);
  not not_116 (not_116_out, o4);
  not not_117 (not_117_out, o5);
  not not_118 (not_118_out, o0);
  not not_119 (not_119_out, o1);
  not not_120 (not_120_out, o2);
  not not_121 (not_121_out, o4);
  not not_122 (not_122_out, o0);
  not not_123 (not_123_out, o1);
  not not_124 (not_124_out, o2);
  not not_125 (not_125_out, o3);
  not not_126 (not_126_out, o4);
  not not_127 (not_127_out, o5);
  not not_128 (not_128_out, f1);
  not not_129 (not_129_out, f3);
  not not_130 (not_130_out, f5);
  not not_131 (not_131_out, o0);
  not not_132 (not_132_out, o1);
  not not_133 (not_133_out, o3);
  not not_134 (not_134_out, o5);
  not not_135 (not_135_out, o0);
  not not_136 (not_136_out, o1);
  not not_137 (not_137_out, o2);
  not not_138 (not_138_out, o3);
  not not_139 (not_139_out, o4);
  not not_140 (not_140_out, o5);
  not not_141 (not_141_out, f1);
  not not_142 (not_142_out, f3);
  not not_143 (not_143_out, o0);
  not not_144 (not_144_out, o1);
  not not_145 (not_145_out, o2);
  not not_146 (not_146_out, o3);
  not not_147 (not_147_out, o5);
  not not_148 (not_148_out, o0);
  not not_149 (not_149_out, o1);
  not not_150 (not_150_out, o2);
  not not_151 (not_151_out, o3);
  not not_152 (not_152_out, o0);
  not not_153 (not_153_out, o1);
  not not_154 (not_154_out, o2);
  not not_155 (not_155_out, o3);
  not not_156 (not_156_out, o4);
  not not_157 (not_157_out, o5);
  not not_158 (not_158_out, f0);
  not not_159 (not_159_out, f1);
  not not_160 (not_160_out, f3);
  not not_161 (not_161_out, f4);
  not not_162 (not_162_out, f5);
  not not_163 (not_163_out, o0);
  not not_164 (not_164_out, o1);
  not not_165 (not_165_out, o2);
  not not_166 (not_166_out, o3);
  not not_167 (not_167_out, o4);
  not not_168 (not_168_out, o5);
  not not_169 (not_169_out, f0);
  not not_170 (not_170_out, f1);
  not not_171 (not_171_out, f4);
  not not_172 (not_172_out, f5);
  and and_13 (\nor , not_100_out, not_101_out, not_102_out, not_103_out, not_104_out, not_105_out, f0, not_106_out, not_107_out, f3, f4, f5);
  and and_14 (lw, o0, not_108_out, not_109_out, not_110_out, o4, o5);
  and and_15 (sw, o0, not_111_out, o2, not_112_out, o4, o5);
  and and_16 (beq, not_113_out, not_114_out, not_115_out, o3, not_116_out, not_117_out);
  and and_17 (bne, not_118_out, not_119_out, not_120_out, o3, not_121_out, o5);
  and and_18 (slt, not_122_out, not_123_out, not_124_out, not_125_out, not_126_out, not_127_out, f0, not_128_out, f2, not_129_out, f4, not_130_out);
  and and_19 (slti, not_131_out, not_132_out, o2, not_133_out, o4, not_134_out);
  and and_20 (sltu, not_135_out, not_136_out, not_137_out, not_138_out, not_139_out, not_140_out, f0, not_141_out, f2, not_142_out, f4, f5);
  and and_21 (jump, not_143_out, not_144_out, not_145_out, not_146_out, o4, not_147_out);
  and and_22 (jmpl, not_148_out, not_149_out, not_150_out, not_151_out, o4, o5);
  and and_23 (jmpr, not_152_out, not_153_out, not_154_out, not_155_out, not_156_out, not_157_out, not_158_out, not_159_out, f2, not_160_out, not_161_out, not_162_out);
  and and_24 (syscall, not_163_out, not_164_out, not_165_out, not_166_out, not_167_out, not_168_out, not_169_out, not_170_out, f2, f3, not_171_out, not_172_out);
endmodule

module ctl_unity (
  input  [5:0] o0_no5,
  input  [5:0] f0_nf5,
  output Alu,
  output mem,
  output other,
  output Jump,
  output Branch,
  output beq,
  output bne,
  output j,
  output jal,
  output jr,
  output syscall,
  output alu_src,
  output reg_dst,
  output reg_write,
  output mem_write,
  output memyoReg,
  output s_i,
  output ext_u,
  output [3:0] out_21
);

  wire decoderrr_1_add, decoderrr_1_addi, decoderrr_1_addiu, decoderrr_1_addu, decoderrr_1_and,
       decoderrr_1_andi, decoderrr_1_nor, decoderrr_1_or, decoderrr_1_ori, decoderrr_1_sll, decoderrr_1_slt,
       decoderrr_1_slti, decoderrr_1_sltu, decoderrr_1_sra, decoderrr_1_srl, decoderrr_1_sub;

  decoderrr decoderrr_1 (
    .o0(o0_no5[5]), .o1(o0_no5[4]), .o2(o0_no5[3]), .o3(o0_no5[2]), .o4(o0_no5[1]), .o5(o0_no5[0]),
    .f0(f0_nf5[5]), .f1(f0_nf5[4]), .f2(f0_nf5[3]), .f3(f0_nf5[2]), .f4(f0_nf5[1]), .f5(f0_nf5[0]),
    .add(decoderrr_1_add), .\nor (decoderrr_1_nor), .lw(memyoReg), .addi(decoderrr_1_addi), .sw(mem_write),
    .addiu(decoderrr_1_addiu), .beq(beq), .bne(bne), .addu(decoderrr_1_addu), .slt(decoderrr_1_slt),
    .\and (decoderrr_1_and), .slti(decoderrr_1_slti), .andi(decoderrr_1_andi), .sltu(decoderrr_1_sltu),
    .sll(decoderrr_1_sll), .jump(j), .jmpl(jal), .sra(decoderrr_1_sra), .jmpr(jr), .srl(decoderrr_1_srl),
    .syscall(syscall), .sub(decoderrr_1_sub), .\or (decoderrr_1_or), .ori(decoderrr_1_ori));
  or u_alu (Alu, decoderrr_1_addi, decoderrr_1_addiu, decoderrr_1_nor, decoderrr_1_and, decoderrr_1_andi, decoderrr_1_or, decoderrr_1_add, decoderrr_1_sll, decoderrr_1_sra, decoderrr_1_srl, decoderrr_1_ori, decoderrr_1_sub);
  or op3 (out_21[3], decoderrr_1_nor, decoderrr_1_slt, decoderrr_1_slti, decoderrr_1_sltu, decoderrr_1_or, decoderrr_1_ori);
  or u_branch (Branch, beq, bne);
  or op2 (out_21[2], decoderrr_1_add, memyoReg, decoderrr_1_addi, mem_write, decoderrr_1_addiu, decoderrr_1_addu, decoderrr_1_and, decoderrr_1_andi, decoderrr_1_sltu, decoderrr_1_sub);
  or op1 (out_21[1], decoderrr_1_nor, decoderrr_1_slt, decoderrr_1_and, decoderrr_1_slti, decoderrr_1_andi, decoderrr_1_srl, decoderrr_1_sub);
  or u_Jump (Jump, j, jal, jr);
  or op0 (out_21[0], decoderrr_1_add, memyoReg, decoderrr_1_addi, mem_write, decoderrr_1_addiu, decoderrr_1_addu, decoderrr_1_slt, decoderrr_1_and, decoderrr_1_slti, decoderrr_1_andi, decoderrr_1_sra);
  or or_1 (ext_u, decoderrr_1_andi, decoderrr_1_ori);
  or u_alu_src (alu_src, decoderrr_1_addiu, decoderrr_1_sll, decoderrr_1_srl, memyoReg, decoderrr_1_addi, mem_write, decoderrr_1_slti, decoderrr_1_andi, decoderrr_1_sra, decoderrr_1_ori);
  or u_mem (mem, memyoReg, mem_write);
  or \u_移位立即数  (s_i, decoderrr_1_srl, decoderrr_1_sra, decoderrr_1_sll);
  or u_reg_dst (reg_dst, decoderrr_1_addu, decoderrr_1_or, decoderrr_1_sub, decoderrr_1_srl, decoderrr_1_add, decoderrr_1_nor, decoderrr_1_slt, decoderrr_1_and, decoderrr_1_sltu, decoderrr_1_sll, decoderrr_1_sra, jr);
  or u_other (other, decoderrr_1_addu, decoderrr_1_slt, decoderrr_1_slti, decoderrr_1_sltu, syscall);
  or u_reg_write (reg_write, memyoReg, decoderrr_1_srl, decoderrr_1_sra, decoderrr_1_sll, decoderrr_1_sltu, decoderrr_1_andi, decoderrr_1_slti, decoderrr_1_add, decoderrr_1_nor, memyoReg, decoderrr_1_addi, decoderrr_1_addiu, decoderrr_1_addu, decoderrr_1_slt, decoderrr_1_and, decoderrr_1_sub, decoderrr_1_or, decoderrr_1_ori, jal);

  // Notes on the sheet:
  //   无符号扩展
  //   mem_write
  //   beq
  //   memtoReg
  //   bne
endmodule

module main (
);

  wire Alu, alu_1_equal, and_1_out, and_2_out, and_3_out, Branch, clk, clock_1_out, comparator_1_eq,
       ctl_unity_1_alu_src, ctl_unity_1_beq, ctl_unity_1_bne, ctl_unity_1_ext_u, ctl_unity_1_mem_write,
       ctl_unity_1_memyoreg, ctl_unity_1_reg_dst, ctl_unity_1_reg_write, ctl_unity_1_s_i,
       ctl_unity_1_syscall, j, jal, jr, Jump, mem, or_1_out, or_2_out, other;
  wire [3:0] ctl_unity_1_out_21;
  wire [4:0] multiplexer_4_out, multiplexer_5_out, multiplexer_6_out;
  wire [27:0] adder_1_out;
  wire [31:0] a0, adder_2_out, adder_3_out, adder_4_out, alu_1_result, bit_extender_1_out,
       bit_extender_2_out, bit_extender_3_out, bit_extender_4_out, bit_extender_5_out, counter_1_q,
       counter_2_q, counter_3_q, counter_4_q, counter_5_q, counter_6_q, multiplexer_1_out, multiplexer_2_out,
       multiplexer_3_out, multiplexer_7_out, multiplexer_8_out, multiplexer_9_out, multiplexer_10_out,
       multiplexer_11_out, ram_1_data, regfile_1_reg1, regfile_1_reg2_2, regfile_1_s1_value, register_1_q,
       shifter_1_out;
  wire [31:2] rom_1_data;
  wire [31:26] rom_1_data_2;

  Multiplexer #(.width(32)) multiplexer_1 (
    .in0({rom_1_data[31:28], adder_1_out}), .in1(multiplexer_3_out), .out(multiplexer_1_out), .sel(or_2_out));  // open: en
  or or_1 (or_1_out, and_2_out, and_1_out);
  Multiplexer #(.width(32)) multiplexer_2 (
    .in0(multiplexer_1_out), .in1(adder_3_out), .out(multiplexer_2_out), .sel(or_1_out));  // open: en
  Register #(.width(32)) register_1 (.D(multiplexer_2_out), .Q(register_1_q), .clk(clk));  // open: en, clr
  Counter #(.width(32), .max('hffffffff)) counter_1 (
    .count(Alu), .Q(counter_1_q), .clk(clk));  // open: load, D, carry, clr
  Counter #(.width(32), .max('hffffffff)) counter_2 (
    .count(other), .Q(counter_2_q), .clk(clk));  // open: load, D, carry, clr
  Counter #(.width(32), .max('hffffffff)) counter_3 (
    .count(mem), .Q(counter_3_q), .clk(clk));  // open: load, D, carry, clr
  Multiplexer #(.width(32)) multiplexer_3 (
    .in0({rom_1_data, 2'b00}), .in1(regfile_1_reg1), .out(multiplexer_3_out), .sel(jr));  // open: en
  Adder #(.width(32)) adder_1 (.a(register_1_q), .b(32'h4), .out({rom_1_data[31:28], adder_1_out}));  // open: cin, cout
  // Probe on counter_1_q
  // Probe on counter_3_q
  ROM #(.addrWidth(10), .dataWidth(32)) rom_1 (
    .addr(register_1_q[11:2]), .data({rom_1_data_2, rom_1_data[27:2]}));  // open: sel
  or or_2 (or_2_out, jal, j, jr);
  Counter #(.width(32), .max('hffffffff)) counter_4 (
    .count(Jump), .Q(counter_4_q), .clk(clk));  // open: load, D, carry, clr
  ctl_unity ctl_unity_1 (
    .o0_no5(rom_1_data_2), .f0_nf5(rom_1_data[7:2]), .Alu(Alu), .Branch(Branch), .Jump(Jump), .mem(mem),
    .other(other), .out_21(ctl_unity_1_out_21), .ext_u(ctl_unity_1_ext_u), .alu_src(ctl_unity_1_alu_src),
    .s_i(ctl_unity_1_s_i), .reg_dst(ctl_unity_1_reg_dst), .reg_write(ctl_unity_1_reg_write),
    .mem_write(ctl_unity_1_mem_write), .memyoReg(ctl_unity_1_memyoreg), .beq(ctl_unity_1_beq),
    .bne(ctl_unity_1_bne), .j(j), .jal(jal), .jr(jr), .syscall(ctl_unity_1_syscall));
  Counter #(.width(32), .max('hffffffff)) counter_5 (
    .count(Branch), .Q(counter_5_q), .clk(clk));  // open: load, D, carry, clr
  Multiplexer #(.width(5)) multiplexer_4 (
    .in0(rom_1_data[27:23]), .in1(rom_1_data[22:18]), .out(multiplexer_4_out), .sel(ctl_unity_1_s_i));  // open: en
  // Probe on counter_4_q
  // Probe on counter_5_q
  Multiplexer #(.width(5)) multiplexer_5 (
    .in0(multiplexer_6_out), .in1({5{1'b1}}), .out(multiplexer_5_out), .sel(jal));  // open: en
  Adder #(.width(32)) adder_2 (.a(counter_2_q), .b(bit_extender_1_out), .out(adder_2_out));  // open: cin, cout
  assign bit_extender_1_out = {{31{1'b0}}, and_3_out};  // Bit_Extender bit_extender_1
  // Probe on adder_2_out
  assign bit_extender_2_out = {{16{rom_1_data[17]}}, rom_1_data[17:2]};  // Bit_Extender bit_extender_2
  assign bit_extender_3_out = {{16{1'b0}}, rom_1_data[17:2]};  // Bit_Extender bit_extender_3
  assign bit_extender_4_out = {{27{1'b0}}, rom_1_data[12:8]};  // Bit_Extender bit_extender_4
  Multiplexer #(.width(5)) multiplexer_6 (
    .in0(rom_1_data[22:18]), .in1(rom_1_data[17:13]), .out(multiplexer_6_out), .sel(ctl_unity_1_reg_dst));  // open: en
  Multiplexer #(.width(32)) multiplexer_7 (
    .in0(bit_extender_2_out), .in1(bit_extender_3_out), .out(multiplexer_7_out), .sel(ctl_unity_1_ext_u));  // open: en
  Shifter #(.width(32)) shifter_1 (.in(bit_extender_2_out), .\dist (5'b00010), .out(shifter_1_out));
  Multiplexer #(.width(32)) multiplexer_8 (
    .in0(multiplexer_11_out), .in1({rom_1_data[31:28], adder_1_out}), .out(multiplexer_8_out), .sel(jal));  // open: en
  Multiplexer #(.width(32)) multiplexer_9 (
    .in0(multiplexer_7_out), .in1(bit_extender_4_out), .out(multiplexer_9_out), .sel(ctl_unity_1_s_i));  // open: en
  Adder #(.width(32)) adder_3 (
    .a(shifter_1_out), .b({rom_1_data[31:28], adder_1_out}), .out(adder_3_out));  // open: cin, cout
  Hex_Digit_Display hex_digit_display_1 (.value(a0[31:28]));  // open: dp
  regfile regfile_1 (
    .Reg1_num(multiplexer_4_out), .Reg2(rom_1_data[22:18]), .Write_Reg_num(multiplexer_5_out),
    .Din(multiplexer_8_out), .Write_Enable(ctl_unity_1_reg_write), .Clock(clk), .Reg1(regfile_1_reg1),
    .Reg2_2(regfile_1_reg2_2), .s0_Value(a0), .s1_Value(regfile_1_s1_value));  // open: s2_Value, ra_Value
  Hex_Digit_Display hex_digit_display_2 (.value(a0[27:24]));  // open: dp
  and and_1 (and_1_out, ctl_unity_1_bne, ~alu_1_equal);  // AND_Gate
  Multiplexer #(.width(32)) multiplexer_10 (
    .in0(regfile_1_reg2_2), .in1(multiplexer_9_out), .out(multiplexer_10_out), .sel(ctl_unity_1_alu_src));  // open: en
  Hex_Digit_Display hex_digit_display_3 (.value(a0[23:20]));  // open: dp
  ALU alu_1 (
    .AluOP(ctl_unity_1_out_21), .X(regfile_1_reg1), .Equal(alu_1_equal), .Result(alu_1_result),
    .Y(multiplexer_10_out));  // open: Signed_Overflow, Result_2, UnSigned_Overflow
  Hex_Digit_Display hex_digit_display_4 (.value(a0[19:16]));  // open: dp
  and and_2 (and_2_out, ctl_unity_1_beq, alu_1_equal);
  Hex_Digit_Display hex_digit_display_5 (.value(a0[15:12]));  // open: dp
  Hex_Digit_Display hex_digit_display_6 (.value(a0[11:8]));  // open: dp
  Clock clock_1 (.out(clock_1_out));
  Hex_Digit_Display hex_digit_display_7 (.value(a0[7:4]));  // open: dp
  RAM #(.addrWidth(10), .dataWidth(32), .bus("separate")) ram_1 (
    .addr(alu_1_result[11:2]), .din(regfile_1_reg2_2), .data(ram_1_data), .str(ctl_unity_1_mem_write),
    .clk(clk), .ld(1'b1));  // open: sel, clr
  or or_3 (clk, clock_1_out, and_3_out);
  Hex_Digit_Display hex_digit_display_8 (.value(a0[3:0]));  // open: dp
  Comparator #(.width(32)) comparator_1 (.a(regfile_1_s1_value), .b(32'ha), .eq(comparator_1_eq));  // open: gt, lt
  Multiplexer #(.width(32)) multiplexer_11 (
    .in0(alu_1_result), .in1(ram_1_data), .out(multiplexer_11_out), .sel(ctl_unity_1_memyoreg));  // open: en
  and and_3 (and_3_out, comparator_1_eq, ctl_unity_1_syscall);
  Counter #(.width(32), .max('hffffffff)) counter_6 (.Q(counter_6_q), .clk(clk));  // open: load, D, count, carry, clr
  assign bit_extender_5_out = {{31{1'b0}}, and_3_out};  // Bit_Extender bit_extender_5
  Adder #(.width(32)) adder_4 (.a(counter_6_q), .b(bit_extender_5_out), .out(adder_4_out));  // open: cin, cout
  // Probe on adder_4_out

  // Notes on the sheet:
  //   contents of rom_1 (hex, n*v repeats v):
  //   20110001 8000c05 20110001 20120002 20130003 8000c09 20110001 20120002 20130003 8000c0d 20110001
  //   20120002 20130003 8000c11 20110001 20120002 20130003 c000cb8 20100001 20110001 118fc0 112020
  //   20020022 c 118882 12200001 8000c15 112020 20020022 c 20110001 118880 112020 20020022 c 12200001
  //   8000c1f 20110001 118fc0 112020 20020022 c 1188c3 112020 20020022 c 118903 112020 20020022 c 118903
  //   112020 20020022 c 118903 112020 20020022 c 118903 112020 20020022 c 118903 112020 20020022 c 118903
  //   112020 20020022 c 118903 112020 20020022 c 20100001 109fc0 139fc3 8021 2012000c 24160003 26100001
  //   3210000f 20080008 20090001 139900 2709825 132020 20020022 c 1094022 1500fff9 22100001 2018000f
  //   2188024 108700 20080008 20090001 139902 2709825 132021 20020022 c 1094022 1500fff9 108702 2c9b022
  //   12c00001 8000c50 4020 1084027 84400 3508ffff 82021 20020022 c 2010ffff 20110000 ae300000 22100001
  //   22310004 ae300000 22100001 22310004 ae300000 22100001 22310004 ae300000 22100001 22310004 ae300000
  //   22100001 22310004 ae300000 22100001 22310004 ae300000 22100001 22310004 ae300000 22100001 22310004
  //   ae300000 22100001 22310004 ae300000 22100001 22310004 ae300000 22100001 22310004 ae300000 22100001
  //   22310004 ae300000 22100001 22310004 ae300000 22100001 22310004 ae300000 22100001 22310004 ae300000
  //   22100001 22310004 22100001 8020 2011003c 8e130000 8e340000 274402a 11000002 ae330000 ae140000
  //   2231fffc 1611fff8 102020 20020022 c 22100004 2011003c 1611fff2 2002000a c 20100000 22100001 102020
  //   20020022 c 22100002 102020 20020022 c 22100003 102020 20020022 c 22100004 102020 20020022 c 22100005
  //   102020 20020022 c 22100006 102020 20020022 c 22100007 102020 20020022 c 22100008 102020 20020022
  //   20020022 c 3e00008
endmodule

module regfile (
  input  [4:0] Reg1_num,
  input  [4:0] Reg2,
  input  [4:0] Write_Reg_num,
  input  [31:0] Din,
  input  Write_Enable,
  input  Clock,
  output [31:0] Reg1,
  output [31:0] s0_Value,
  output [31:0] s1_Value,
  output [31:0] s2_Value,
  output [31:0] ra_Value,
  output [31:0] Reg2_2
);

  wire _00, _01, _02, _03, _04, _05, _06, _07, _08, _09, _10, _11, _12, _13, _14, _15, _16, _17, _18, _19,
       _20, _21, _22, _23, _24, _25, _26, _27, _28, _29, _30, _31;
  wire [31:0] _1_q, _3_q, _5_q, _6_q, _7_q, _8_q, _9_q, _10_q, _11_q, _12_q, _13_q, _14_q, _15_q, _16_q,
       _17_q, _19_q, _20_q, _21_q, _22_q, _23_q, _24_q, _25_q, _26_q, _27_q, _28_q, _29_q, _30_q,
       demultiplexer_2_out0, demultiplexer_2_out1, demultiplexer_2_out2, demultiplexer_2_out3,
       demultiplexer_2_out4, demultiplexer_2_out5, demultiplexer_2_out6, demultiplexer_2_out7,
       demultiplexer_2_out8, demultiplexer_2_out9, demultiplexer_2_out10, demultiplexer_2_out11,
       demultiplexer_2_out12, demultiplexer_2_out13, demultiplexer_2_out14, demultiplexer_2_out15,
       demultiplexer_2_out16, demultiplexer_2_out17, demultiplexer_2_out18, demultiplexer_2_out19,
       demultiplexer_2_out20, demultiplexer_2_out21, demultiplexer_2_out22, demultiplexer_2_out23,
       demultiplexer_2_out24, demultiplexer_2_out25, demultiplexer_2_out26, demultiplexer_2_out27,
       demultiplexer_2_out28, demultiplexer_2_out29, demultiplexer_2_out30, demultiplexer_2_out31;

  Multiplexer #(.select(5), .width(32)) multiplexer_1 (
    .in0({32{1'b0}}), .in1(_1_q), .in2(s1_Value), .in3(_3_q), .in4(s0_Value), .in5(_5_q), .in6(_6_q),
    .in7(_7_q), .in8(_8_q), .in9(_9_q), .in10(_10_q), .in11(_11_q), .in12(_12_q), .in13(_13_q), .in14(_14_q),
    .in15(_15_q), .in16(_16_q), .in17(_17_q), .in18(s2_Value), .in19(_19_q), .in20(_20_q), .in21(_21_q),
    .in22(_22_q), .in23(_23_q), .in24(_24_q), .in25(_25_q), .in26(_26_q), .in27(_27_q), .in28(_28_q),
    .in29(_29_q), .in30(_30_q), .in31(ra_Value), .out(Reg1), .sel(Reg1_num), .en(1'b1));
  Demultiplexer #(.select(5)) demultiplexer_1 (
    .out0(_00), .out1(_01), .out2(_02), .out3(_03), .out4(_04), .out5(_05), .out6(_06), .out7(_07),
    .out8(_08), .out9(_09), .out10(_10), .out11(_11), .out12(_12), .out13(_13), .out14(_14), .out15(_15),
    .out16(_16), .out17(_17), .out18(_18), .out19(_19), .out20(_20), .out21(_21), .out22(_22), .out23(_23),
    .out24(_24), .out25(_25), .out26(_26), .out27(_27), .out28(_28), .out29(_29), .out30(_30), .out31(_31),
    .in(Write_Enable), .sel(Write_Reg_num), .en(1'b1));
  Register #(.width(32)) _1 (.D(demultiplexer_2_out1), .en(_01), .Q(_1_q), .clk(Clock));  // open: clr
  Register #(.width(32)) u__16 (.D(demultiplexer_2_out16), .en(_16), .Q(_16_q), .clk(Clock));  // open: clr
  Register #(.width(32)) u__17 (.D(demultiplexer_2_out17), .en(_17), .Q(_17_q), .clk(Clock));  // open: clr
  Register #(.width(32)) _2 (.D(demultiplexer_2_out2), .en(_02), .Q(s1_Value), .clk(Clock));  // open: clr
  Register #(.width(32)) u__18 (.D(demultiplexer_2_out18), .en(_18), .Q(s2_Value), .clk(Clock));  // open: clr
  Register #(.width(32)) _4 (.D(demultiplexer_2_out4), .en(_04), .Q(s0_Value), .clk(Clock));  // open: clr
  Register #(.width(32)) _3 (.D(demultiplexer_2_out3), .en(_03), .Q(_3_q), .clk(Clock));  // open: clr
  Register #(.width(32)) u__19 (.D(demultiplexer_2_out19), .en(_19), .Q(_19_q), .clk(Clock));  // open: clr
  Register #(.width(32)) _5 (.D(demultiplexer_2_out5), .en(_05), .Q(_5_q), .clk(Clock));  // open: clr
  Register #(.width(32)) u__20 (.D(demultiplexer_2_out20), .en(_20), .Q(_20_q), .clk(Clock));  // open: clr
  Register #(.width(32)) u__21 (.D(demultiplexer_2_out21), .en(_21), .Q(_21_q), .clk(Clock));  // open: clr
  Demultiplexer #(.select(5), .width(32)) demultiplexer_2 (
    .out0(demultiplexer_2_out0), .out1(demultiplexer_2_out1), .out2(demultiplexer_2_out2),
    .out3(demultiplexer_2_out3), .out4(demultiplexer_2_out4), .out5(demultiplexer_2_out5),
    .out6(demultiplexer_2_out6), .out7(demultiplexer_2_out7), .out8(demultiplexer_2_out8),
    .out9(demultiplexer_2_out9), .out10(demultiplexer_2_out10), .out11(demultiplexer_2_out11),
    .out12(demultiplexer_2_out12), .out13(demultiplexer_2_out13), .out14(demultiplexer_2_out14),
    .out15(demultiplexer_2_out15), .out16(demultiplexer_2_out16), .out17(demultiplexer_2_out17),
    .out18(demultiplexer_2_out18), .out19(demultiplexer_2_out19), .out20(demultiplexer_2_out20),
    .out21(demultiplexer_2_out21), .out22(demultiplexer_2_out22), .out23(demultiplexer_2_out23),
    .out24(demultiplexer_2_out24), .out25(demultiplexer_2_out25), .out26(demultiplexer_2_out26),
    .out27(demultiplexer_2_out27), .out28(demultiplexer_2_out28), .out29(demultiplexer_2_out29),
    .out30(demultiplexer_2_out30), .out31(demultiplexer_2_out31), .in(Din), .sel(Write_Reg_num), .en(1'b1));
  Register #(.width(32)) _6 (.D(demultiplexer_2_out6), .en(_06), .Q(_6_q), .clk(Clock));  // open: clr
  Register #(.width(32)) u__22 (.D(demultiplexer_2_out22), .en(_22), .Q(_22_q), .clk(Clock));  // open: clr
  Register #(.width(32)) u__23 (.D(demultiplexer_2_out23), .en(_23), .Q(_23_q), .clk(Clock));  // open: clr
  Register #(.width(32)) _8 (.D(demultiplexer_2_out8), .en(_08), .Q(_8_q), .clk(Clock));  // open: clr
  Register #(.width(32)) _7 (.D(demultiplexer_2_out7), .en(_07), .Q(_7_q), .clk(Clock));  // open: clr
  Register #(.width(32)) u__24 (.D(demultiplexer_2_out24), .en(_24), .Q(_24_q), .clk(Clock));  // open: clr
  Register #(.width(32)) _9 (.D(demultiplexer_2_out9), .en(_09), .Q(_9_q), .clk(Clock));  // open: clr
  Register #(.width(32)) u__25 (.D(demultiplexer_2_out25), .en(_25), .Q(_25_q), .clk(Clock));  // open: clr
  Register #(.width(32)) u__10 (.D(demultiplexer_2_out10), .en(_10), .Q(_10_q), .clk(Clock));  // open: clr
  Register #(.width(32)) u__11 (.D(demultiplexer_2_out11), .en(_11), .Q(_11_q), .clk(Clock));  // open: clr
  Register #(.width(32)) u__26 (.D(demultiplexer_2_out26), .en(_26), .Q(_26_q), .clk(Clock));  // open: clr
  Register #(.width(32)) u__27 (.D(demultiplexer_2_out27), .en(_27), .Q(_27_q), .clk(Clock));  // open: clr
  Register #(.width(32)) u__12 (.D(demultiplexer_2_out12), .en(_12), .Q(_12_q), .clk(Clock));  // open: clr
  Register #(.width(32)) u__28 (.D(demultiplexer_2_out28), .en(_28), .Q(_28_q), .clk(Clock));  // open: clr
  Register #(.width(32)) u__14 (.D(demultiplexer_2_out14), .en(_14), .Q(_14_q), .clk(Clock));  // open: clr
  Register #(.width(32)) u__13 (.D(demultiplexer_2_out13), .en(_13), .Q(_13_q), .clk(Clock));  // open: clr
  Register #(.width(32)) u__29 (.D(demultiplexer_2_out29), .en(_29), .Q(_29_q), .clk(Clock));  // open: clr
  Register #(.width(32)) u__15 (.D(demultiplexer_2_out15), .en(_15), .Q(_15_q), .clk(Clock));  // open: clr
  Register #(.width(32)) u__30 (.D(demultiplexer_2_out30), .en(_30), .Q(_30_q), .clk(Clock));  // open: clr
  Register #(.width(32)) u__31 (.D(demultiplexer_2_out31), .en(_31), .Q(ra_Value), .clk(Clock));  // open: clr
  Multiplexer #(.select(5), .width(32)) multiplexer_2 (
    .in0({32{1'b0}}), .in1(_1_q), .in2(s1_Value), .in3(_3_q), .in4(s0_Value), .in5(_5_q), .in6(_6_q),
    .in7(_7_q), .in8(_8_q), .in9(_9_q), .in10(_10_q), .in11(_11_q), .in12(_12_q), .in13(_13_q), .in14(_14_q),
    .in15(_15_q), .in16(_16_q), .in17(_17_q), .in18(s2_Value), .in19(_19_q), .in20(_20_q), .in21(_21_q),
    .in22(_22_q), .in23(_23_q), .in24(_24_q), .in25(_25_q), .in26(_26_q), .in27(_27_q), .in28(_28_q),
    .in29(_29_q), .in30(_30_q), .in31(ra_Value), .out(Reg2_2), .sel(Reg2), .en(1'b1));

  // Other names for the same wires on the sheet: clk = Clock; ra[31:0] = ra_Value; reg2_num[4:0] = Reg2;
  //   reg2_t[31:0] = Reg2_2; s0[31:0] = s0_Value; s1[31:0] = s1_Value; s2[31:0] = s2_Value; WE = Write_Enable;
  //   write_data[31:0] = Din

  // Notes on the sheet:
  //   输入引脚
  //   输出引脚
  //   Debug引脚，便于观测寄存器值
  //   请勿修改引脚以及封装，直接使用隧道连接电路
endmodule
