// Logisim project regfile.circ as structural Verilog: 3 circuits, main circuit main
module main (
  input  [4:0] Reg1_num,
  input  [4:0] Reg2,
  input  [4:0] Write_Reg_num,
  input  [31:0] Din,
  input  Write_Enable,
  input  Clock,
  output [31:0] Reg1,
  output [31:0] s0_Value,
  output [31:0] s1_Value,
  output [31:0] s2_Value,
  output [31:0] ra_Value,
  output [31:0] Reg2_2
);

  wire _00, _01, _02, _03, _04, _05, _06, _07, _08, _09, _10, _11, _12, _13, _14, _15, _16, _17, _18, _19,
       _20, _21, _22, _23, _24, _25, _26, _27, _28, _29, _30, _31;
  wire [31:0] _1_q, _2_q, _3_q, _4_q, _5_q, _6_q, _7_q, _8_q, _9_q, _10_q, _11_q, _12_q, _13_q, _14_q, _15_q,
       _19_q, _20_q, _21_q, _22_q, _23_q, _24_q, _25_q, _26_q, _27_q, _28_q, _29_q, _30_q,
       demultiplexer_2_out0, demultiplexer_2_out1, demultiplexer_2_out2, demultiplexer_2_out3,
       demultiplexer_2_out4, demultiplexer_2_out5, demultiplexer_2_out6, demultiplexer_2_out7,
       demultiplexer_2_out8, demultiplexer_2_out9, demultiplexer_2_out10, demultiplexer_2_out11,
       demultiplexer_2_out12, demultiplexer_2_out13, demultiplexer_2_out14, demultiplexer_2_out15,
       demultiplexer_2_out16, demultiplexer_2_out17, demultiplexer_2_out18, demultiplexer_2_out19,
       demultiplexer_2_out20, demultiplexer_2_out21, demultiplexer_2_out22, demultiplexer_2_out23,
       demultiplexer_2_out24, demultiplexer_2_out25, demultiplexer_2_out26, demultiplexer_2_out27,
       demultiplexer_2_out28, demultiplexer_2_out29, demultiplexer_2_out30, demultiplexer_2_out31;

  Multiplexer #(.select(5), .width(32)) multiplexer_1 (
    .in0({32{1'b0}}), .in1(_1_q), .in2(_2_q), .in3(_3_q), .in4(_4_q), .in5(_5_q), .in6(_6_q), .in7(_7_q),
    .in8(_8_q), .in9(_9_q), .in10(_10_q), .in11(_11_q), .in12(_12_q), .in13(_13_q), .in14(_14_q),
    .in15(_15_q), .in16(s0_Value), .in17(s1_Value), .in18(s2_Value), .in19(_19_q), .in20(_20_q),
    .in21(_21_q), .in22(_22_q), .in23(_23_q), .in24(_24_q), .in25(_25_q), .in26(_26_q), .in27(_27_q),
    .in28(_28_q), .in29(_29_q), .in30(_30_q), .in31(ra_Value), .out(Reg1), .sel(Reg1_num), .en(1'b1));
  Demultiplexer #(.select(5)) demultiplexer_1 (
    .out0(_00), .out1(_01), .out2(_02), .out3(_03), .out4(_04), .out5(_05), .out6(_06), .out7(_07),
    .out8(_08), .out9(_09), .out10(_10), .out11(_11), .out12(_12), .out13(_13), .out14(_14), .out15(_15),
    .out16(_16), .out17(_17), .out18(_18), .out19(_19), .out20(_20), .out21(_21), .out22(_22), .out23(_23),
    .out24(_24), .out25(_25), .out26(_26), .out27(_27), .out28(_28), .out29(_29), .out30(_30), .out31(_31),
    .in(Write_Enable), .sel(Write_Reg_num), .en(1'b1));
  Register #(.width(32)) _1 (.D(demultiplexer_2_out1), .en(_01), .Q(_1_q), .clk(Clock));  // open: clr
  Register #(.width(32)) u__16 (.D(demultiplexer_2_out16), .en(_16), .Q(s0_Value), .clk(Clock));  // open: clr
  Register #(.width(32)) u__17 (.D(demultiplexer_2_out17), .en(_17), .Q(s1_Value), .clk(Clock));  // open: clr
  Register #(.width(32)) _2 (.D(demultiplexer_2_out2), .en(_02), .Q(_2_q), .clk(Clock));  // open: clr
  Register #(.width(32)) u__18 (.D(demultiplexer_2_out18), .en(_18), .Q(s2_Value), .clk(Clock));  // open: clr
  Register #(.width(32)) _4 (.D(demultiplexer_2_out4), .en(_04), .Q(_4_q), .clk(Clock));  // open: clr
  Register #(.width(32)) _3 (.D(demultiplexer_2_out3), .en(_03), .Q(_3_q), .clk(Clock));  // open: clr
  Register #(.width(32)) u__19 (.D(demultiplexer_2_out19), .en(_19), .Q(_19_q), .clk(Clock));  // open: clr
  Register #(.width(32)) _5 (.D(demultiplexer_2_out5), .en(_05), .Q(_5_q), .clk(Clock));  // open: clr
  Register #(.width(32)) u__20 (.D(demultiplexer_2_out20), .en(_20), .Q(_20_q), .clk(Clock));  // open: clr
  Register #(.width(32)) u__21 (.D(demultiplexer_2_out21), .en(_21), .Q(_21_q), .clk(Clock));  // open: clr
  Demultiplexer #(.select(5), .width(32)) demultiplexer_2 (
    .out0(demultiplexer_2_out0), .out1(demultiplexer_2_out1), .out2(demultiplexer_2_out2),
    .out3(demultiplexer_2_out3), .out4(demultiplexer_2_out4), .out5(demultiplexer_2_out5),
    .out6(demultiplexer_2_out6), .out7(demultiplexer_2_out7), .out8(demultiplexer_2_out8),
    .out9(demultiplexer_2_out9), .out10(demultiplexer_2_out10), .out11(demultiplexer_2_out11),
    .out12(demultiplexer_2_out12), .out13(demultiplexer_2_out13), .out14(demultiplexer_2_out14),
    .out15(demultiplexer_2_out15), .out16(demultiplexer_2_out16), .out17(demultiplexer_2_out17),
    .out18(demultiplexer_2_out18), .out19(demultiplexer_2_out19), .out20(demultiplexer_2_out20),
    .out21(demultiplexer_2_out21), .out22(demultiplexer_2_out22), .out23(demultiplexer_2_out23),
    .out24(demultiplexer_2_out24), .out25(demultiplexer_2_out25), .out26(demultiplexer_2_out26),
    .out27(demultiplexer_2_out27), .out28(demultiplexer_2_out28), .out29(demultiplexer_2_out29),
    .out30(demultiplexer_2_out30), .out31(demultiplexer_2_out31), .in(Din), .sel(Write_Reg_num), .en(1'b1));
  Register #(.width(32)) _6 (.D(demultiplexer_2_out6), .en(_06), .Q(_6_q), .clk(Clock));  // open: clr
  Register #(.width(32)) u__22 (.D(demultiplexer_2_out22), .en(_22), .Q(_22_q), .clk(Clock));  // open: clr
  Register #(.width(32)) u__23 (.D(demultiplexer_2_out23), .en(_23), .Q(_23_q), .clk(Clock));  // open: clr
  Register #(.width(32)) _8 (.D(demultiplexer_2_out8), .en(_08), .Q(_8_q), .clk(Clock));  // open: clr
  Register #(.width(32)) _7 (.D(demultiplexer_2_out7), .en(_07), .Q(_7_q), .clk(Clock));  // open: clr
  Register #(.width(32)) u__24 (.D(demultiplexer_2_out24), .en(_24), .Q(_24_q), .clk(Clock));  // open: clr
  Register #(.width(32)) _9 (.D(demultiplexer_2_out9), .en(_09), .Q(_9_q), .clk(Clock));  // open: clr
  Register #(.width(32)) u__25 (.D(demultiplexer_2_out25), .en(_25), .Q(_25_q), .clk(Clock));  // open: clr
  Register #(.width(32)) u__10 (.D(demultiplexer_2_out10), .en(_10), .Q(_10_q), .clk(Clock));  // open: clr
  Register #(.width(32)) u__11 (.D(demultiplexer_2_out11), .en(_11), .Q(_11_q), .clk(Clock));  // open: clr
  Register #(.width(32)) u__26 (.D(demultiplexer_2_out26), .en(_26), .Q(_26_q), .clk(Clock));  // open: clr
  Register #(.width(32)) u__27 (.D(demultiplexer_2_out27), .en(_27), .Q(_27_q), .clk(Clock));  // open: clr
  Register #(.width(32)) u__12 (.D(demultiplexer_2_out12), .en(_12), .Q(_12_q), .clk(Clock));  // open: clr
  Register #(.width(32)) u__28 (.D(demultiplexer_2_out28), .en(_28), .Q(_28_q), .clk(Clock));  // open: clr
  Register #(.width(32)) u__14 (.D(demultiplexer_2_out14), .en(_14), .Q(_14_q), .clk(Clock));  // open: clr
  Register #(.width(32)) u__13 (.D(demultiplexer_2_out13), .en(_13), .Q(_13_q), .clk(Clock));  // open: clr
  Register #(.width(32)) u__29 (.D(demultiplexer_2_out29), .en(_29), .Q(_29_q), .clk(Clock));  // open: clr
  Register #(.width(32)) u__15 (.D(demultiplexer_2_out15), .en(_15), .Q(_15_q), .clk(Clock));  // open: clr
  Register #(.width(32)) u__30 (.D(demultiplexer_2_out30), .en(_30), .Q(_30_q), .clk(Clock));  // open: clr
  Register #(.width(32)) u__31 (.D(demultiplexer_2_out31), .en(_31), .Q(ra_Value), .clk(Clock));  // open: clr
  Multiplexer #(.select(5), .width(32)) multiplexer_2 (
    .in0({32{1'b0}}), .in1(_1_q), .in2(_2_q), .in3(_3_q), .in4(_4_q), .in5(_5_q), .in6(_6_q), .in7(_7_q),
    .in8(_8_q), .in9(_9_q), .in10(_10_q), .in11(_11_q), .in12(_12_q), .in13(_13_q), .in14(_14_q),
    .in15(_15_q), .in16(s0_Value), .in17(s1_Value), .in18(s2_Value), .in19(_19_q), .in20(_20_q),
    .in21(_21_q), .in22(_22_q), .in23(_23_q), .in24(_24_q), .in25(_25_q), .in26(_26_q), .in27(_27_q),
    .in28(_28_q), .in29(_29_q), .in30(_30_q), .in31(ra_Value), .out(Reg2_2), .sel(Reg2), .en(1'b1));

  // Other names for the same wires on the sheet: clk = Clock; ra[31:0] = ra_Value; reg2_num[4:0] = Reg2;
  //   reg2_t[31:0] = Reg2_2; s0[31:0] = s0_Value; s1[31:0] = s1_Value; s2[31:0] = s2_Value; WE = Write_Enable;
  //   write_data[31:0] = Din

  // Notes on the sheet:
  //   输入引脚
  //   输出引脚
  //   Debug引脚，便于观测寄存器值
  //   请勿修改引脚以及封装，直接使用隧道连接电路
endmodule

module test (
);

  wire undriven;

  main main_1 (.Clock(undriven));  // open: Reg1_num, Reg2, Write_Reg_num, Din, Write_Enable, Reg1, Reg2_2, s0_Value, s1_Value, s2_Value, ra_Value
endmodule

module Auto_cal (
  output [31:0] out_1,
  output [31:0] out_2
);

  wire clock_1_out, clock_2_out, comparator_1_eq, comparator_2_eq, not_1_out, not_2_out, not_3_out,
       not_4_out, or_1_out;
  wire [3:0] multiplexer_4_out, multiplexer_4_out_2, multiplexer_4_out_4, multiplexer_4_out_5,
       multiplexer_4_out_6, multiplexer_4_out_7, multiplexer_4_out_8;
  wire [5:0] adder_1_out, addr, count;
  wire [11:8] multiplexer_4_out_3;
  wire [31:0] alu_1_p4, main_1_reg2_2, multiplexer_2_out, ram_1_data;

  // Probe on addr
  // Probe on count
  // Probe on out_1
  Counter #(.width(6), .max('h3f)) counter_1 (
    .load(1'b0), .count(1'b1), .Q(count), .clk(or_1_out));  // open: D, carry, clr
  or or_1 (or_1_out, clock_1_out, comparator_2_eq);
  Clock #(.highDuration(4), .lowDuration(4)) clock_1 (.out(clock_1_out));
  Comparator #(.width(6)) comparator_1 (.a({6{1'b0}}), .b(count), .eq(comparator_1_eq));  // open: gt, lt
  Adder #(.width(6)) adder_1 (.a(6'b011111), .b(count), .out(adder_1_out));  // open: cin, cout
  // Probe on out_2
  Multiplexer #(.width(6)) multiplexer_1 (.in0(adder_1_out), .in1(count), .out(addr), .sel(not_1_out));  // open: en
  not not_1 (not_1_out, or_1_out);
  Comparator #(.width(6)) comparator_2 (.a(count), .b(6'b100000), .eq(comparator_2_eq));  // open: gt, lt
  Multiplexer #(.width(32)) multiplexer_2 (
    .in0(out_2), .in1(ram_1_data), .out(multiplexer_2_out), .sel(not_2_out));  // open: en
  not not_2 (not_2_out, or_1_out);
  not not_3 (not_3_out, clock_2_out);
  Clock clock_2 (.out(clock_2_out));
  Hex_Digit_Display hex_digit_display_1 (.value(multiplexer_4_out_8));  // open: dp
  RAM #(.addrWidth(6), .dataWidth(32), .bus("separate")) ram_1 (
    .addr(addr), .din(multiplexer_2_out), .data(ram_1_data), .str(or_1_out), .clk(not_3_out), .ld(not_4_out));  // open: sel, clr
  not not_4 (not_4_out, or_1_out);
  Hex_Digit_Display hex_digit_display_2 (.value(multiplexer_4_out_6));  // open: dp
  Hex_Digit_Display hex_digit_display_3 (.value(multiplexer_4_out_7));  // open: dp
  Hex_Digit_Display hex_digit_display_4 (.value(multiplexer_4_out_5));  // open: dp
  main main_1 (
    .Reg2(5'b01101), .Write_Reg_num(5'b01101), .Din(alu_1_p4), .Write_Enable(1'b1), .Clock(or_1_out),
    .Reg2_2(main_1_reg2_2));  // open: Reg1_num, Reg1, s0_Value, s1_Value, s2_Value, ra_Value
  Hex_Digit_Display hex_digit_display_5 (.value(multiplexer_4_out_4));  // open: dp
  Multiplexer #(.width(32)) multiplexer_3 (
    .in0(main_1_reg2_2), .in1({32{1'b0}}), .out(out_2), .sel(comparator_1_eq));  // open: en
  Register #(.width(32)) register_1 (.D(ram_1_data), .Q(out_1), .clk(not_3_out));  // open: en, clr
  Hex_Digit_Display hex_digit_display_6 (.value(multiplexer_4_out_2));  // open: dp
  Hex_Digit_Display hex_digit_display_7 (.value(multiplexer_4_out_3));  // open: dp
  // ALU alu_1: pin names not known; wires that end beside it: out_2, out_1, 4'b0101, alu_1_p4
  Hex_Digit_Display hex_digit_display_8 (.value(multiplexer_4_out));  // open: dp
  Multiplexer #(.width(32)) multiplexer_4 (
    .in1(out_2),
    .out({multiplexer_4_out_8, multiplexer_4_out_7, multiplexer_4_out_6, multiplexer_4_out_5, multiplexer_4_out_4, multiplexer_4_out_3, multiplexer_4_out_2, multiplexer_4_out}),
    .sel(comparator_2_eq));  // open: in0, en

  // Other names for the same wires on the sheet: data[31:0] = out_1; temp[31:0] = out_2
endmodule
